// Logisim project lab1.circ as structural Verilog: 1 circuit, main circuit main
module main (
  input  x,
  input  s,
  input  y,
  input  a1,
  input  b1,
  input  c1,
  input  b2,
  input  a2,
  input  c2,
  output f1,
  output f2,
  output f3
);

  wire and_1_out, and_2_out, and_3_out, not_1_out, not_2_out, not_3_out, not_4_out, not_5_out, or_1_out,
       or_2_out;

  not not_1 (not_1_out, s);
  not not_2 (not_2_out, a2);
  and and_1 (and_1_out, x, not_1_out);
  or or_1 (or_1_out, a1, b1);
  not not_3 (not_3_out, b1);
  not not_4 (not_4_out, b2);
  or or_2 (or_2_out, not_2_out, c2);
  and and_2 (and_2_out, s, y);
  not not_5 (not_5_out, or_1_out);
  and and_3 (and_3_out, not_3_out, c1);
  and and_4 (f3, not_4_out, or_2_out);
  or or_3 (f1, and_1_out, and_2_out);
  or or_4 (f2, not_5_out, and_3_out);
endmodule
