// Logisim project 7bar.circ as structural Verilog: 8 circuits, main circuit main
module main (
  input  c3,
  input  c2,
  input  c1,
  input  c0
);

  wire H0_1_p5, H1_1_p5, H2_1_bar2, H3_1_bar3, H4_1_bar4, H5_1_bar5, H6_1_bar6;

  // H0 H0_1: pin names not known; wires that end beside it: c3, c2, c1, c0, H0_1_p5
  // H1 H1_1: pin names not known; wires that end beside it: c3, c2, c1, c0, H1_1_p5
  H2 H2_1 (.c3(c3), .c2(c2), .c1(c1), .c0(c0), .bar2(H2_1_bar2));
  H3 H3_1 (.c3(c3), .c2(c2), .c1(c1), .c0(c0), .bar3(H3_1_bar3));
  H4 H4_1 (.c3(c3), .c2(c2), .c1(c1), .c0(c0), .bar4(H4_1_bar4));
  H5 H5_1 (.c3(c3), .c2(c2), .c1(c1), .c0(c0), .bar5(H5_1_bar5));
  H6 H6_1 (.c3(c3), .c2(c2), .c1(c1), .c0(c0), .bar6(H6_1_bar6));
  _7_Segment_Display L_7_Segment_Display_1 (
    .g(H6_1_bar6), .f(H5_1_bar5), .a(H0_1_p5), .b(H1_1_p5), .e(H4_1_bar4), .d(H3_1_bar3), .c(H2_1_bar2));  // open: dp
endmodule

module H0 (
  input  c3,
  input  c2,
  input  c1,
  input  c0,
  output bar0
);

  wire and_1_out, and_2_out, and_3_out, and_4_out, and_5_out, and_6_out, not_1_out, not_2_out, not_3_out,
       not_4_out;

  not not_1 (not_1_out, c3);
  not not_2 (not_2_out, c2);
  not not_3 (not_3_out, c0);
  and and_1 (and_1_out, not_1_out, c1);
  and and_2 (and_2_out, not_2_out, not_3_out);
  and and_3 (and_3_out, c2, c1);
  not not_4 (not_4_out, c1);
  and and_4 (and_4_out, c3, not_3_out);
  and and_5 (and_5_out, not_1_out, c2, c0);
  and and_6 (and_6_out, c3, not_2_out, not_4_out);
  or or_1 (bar0, and_1_out, and_4_out, and_5_out, and_6_out, and_2_out, and_3_out);
endmodule

module H1 (
  input  c3,
  input  c2,
  input  c1,
  input  c0,
  output bar1
);

  wire and_1_out, and_2_out, and_3_out, and_4_out, and_5_out, not_1_out, not_2_out, not_3_out, not_4_out;

  not not_1 (not_1_out, c3);
  not not_2 (not_2_out, c2);
  not not_3 (not_3_out, c1);
  not not_4 (not_4_out, c0);
  and and_1 (and_1_out, not_1_out, not_2_out);
  and and_2 (and_2_out, not_2_out, not_4_out);
  and and_3 (and_3_out, not_1_out, c1, c0);
  and and_4 (and_4_out, not_1_out, not_3_out, not_4_out);
  and and_5 (and_5_out, c3, c0, not_3_out);
  or or_1 (bar1, and_5_out, and_1_out, and_3_out, and_4_out, and_2_out);
endmodule

module H2 (
  input  c3,
  input  c2,
  input  c1,
  input  c0,
  output bar2
);

  wire and_1_out, and_2_out, and_3_out, and_4_out, and_5_out, not_1_out, not_2_out, not_3_out;

  not not_1 (not_1_out, c3);
  not not_2 (not_2_out, c2);
  not not_3 (not_3_out, c1);
  and and_1 (and_1_out, not_1_out, not_3_out);
  and and_2 (and_2_out, not_1_out, c0);
  and and_3 (and_3_out, not_3_out, c0);
  and and_4 (and_4_out, not_1_out, c2);
  and and_5 (and_5_out, c3, not_2_out);
  or or_1 (bar2, and_1_out, and_2_out, and_3_out, and_4_out, and_5_out);
endmodule

module H3 (
  input  c3,
  input  c2,
  input  c1,
  input  c0,
  output bar3
);

  wire and_1_out, and_2_out, and_3_out, and_4_out, and_5_out, not_1_out, not_2_out, not_3_out, not_4_out;

  not not_1 (not_1_out, c2);
  not not_2 (not_2_out, c0);
  not not_3 (not_3_out, c3);
  not not_4 (not_4_out, c1);
  and and_1 (and_1_out, not_1_out, c0, c1);
  and and_2 (and_2_out, not_3_out, not_1_out, not_2_out);
  and and_3 (and_3_out, c2, c0, not_4_out);
  and and_4 (and_4_out, c2, c1, not_2_out);
  and and_5 (and_5_out, c3, not_4_out);
  or or_1 (bar3, and_2_out, and_1_out, and_3_out, and_4_out, and_5_out);
endmodule

module H4 (
  input  c3,
  input  c2,
  input  c1,
  input  c0,
  output bar4
);

  wire and_1_out, and_2_out, and_3_out, and_4_out, not_2_out, not_3_out;

  // NOT_Gate not_1 has open pins: in=c1, out=open
  not not_2 (not_2_out, c0);
  not not_3 (not_3_out, c2);
  and and_1 (and_1_out, not_3_out, not_2_out);
  and and_2 (and_2_out, c1, not_2_out);
  and and_3 (and_3_out, c3, c1);
  and and_4 (and_4_out, c3, c2);
  or or_1 (bar4, and_1_out, and_2_out, and_3_out, and_4_out);
endmodule

module H5 (
  input  c3,
  input  c2,
  input  c1,
  input  c0,
  output bar5
);

  wire and_1_out, and_2_out, and_3_out, and_4_out, and_5_out, not_1_out, not_2_out, not_3_out, not_4_out;

  not not_1 (not_1_out, c3);
  not not_2 (not_2_out, c1);
  not not_3 (not_3_out, c2);
  not not_4 (not_4_out, c0);
  and and_1 (and_1_out, not_2_out, not_4_out);
  and and_2 (and_2_out, not_1_out, c2, not_2_out);
  and and_3 (and_3_out, c2, not_4_out);
  and and_4 (and_4_out, c3, not_3_out);
  and and_5 (and_5_out, c3, c1);
  or or_1 (bar5, and_1_out, and_2_out, and_3_out, and_4_out, and_5_out);
endmodule

module H6 (
  input  c3,
  input  c2,
  input  c1,
  input  c0,
  output bar6
);

  wire and_1_out, and_2_out, and_3_out, and_4_out, and_5_out, not_1_out, not_2_out, not_3_out, not_4_out;

  not not_1 (not_1_out, c2);
  not not_2 (not_2_out, c1);
  not not_3 (not_3_out, c0);
  not not_4 (not_4_out, c3);
  and and_1 (and_1_out, not_1_out, c1);
  and and_2 (and_2_out, c1, not_3_out);
  and and_3 (and_3_out, c3, not_1_out);
  and and_4 (and_4_out, c3, c0);
  and and_5 (and_5_out, not_4_out, not_2_out, c2);
  or or_1 (bar6, and_1_out, and_2_out, and_3_out, and_4_out, and_5_out);
endmodule
