// Logisim project mux.circ as structural Verilog: 3 circuits, main circuit main
module main (
  input  SW_0,
  input  SW_1,
  input  SW_9,
  input  u,
  input  v,
  input  w,
  input  x,
  input  s0,
  input  s1,
  output LEDR_9,
  output m
);

  mux2to1 b (.x(SW_0), .y(SW_1), .s(SW_9), .m(LEDR_9));
  mux4to1 mux4to1_1 (.u(u), .v(v), .w(w), .x(x), .s0(s0), .s1(s1), .m(m));
endmodule

module mux2to1 (
  input  x,
  input  y,
  input  s,
  output m
);

  Multiplexer #(.enable("false")) multiplexer_1 (.in0(x), .in1(y), .out(m), .sel(s));
endmodule

module mux4to1 (
  input  u,
  input  v,
  input  w,
  input  x,
  input  s0,
  input  s1,
  output m
);

  wire multiplexer_1_out, multiplexer_2_out;

  Multiplexer #(.enable("false")) multiplexer_1 (.in0(u), .in1(v), .out(multiplexer_1_out), .sel(s0));
  Multiplexer #(.enable("false")) multiplexer_2 (.in0(w), .in1(x), .out(multiplexer_2_out), .sel(s0));
  Multiplexer #(.enable("false")) multiplexer_3 (.in0(multiplexer_1_out), .in1(multiplexer_2_out), .out(m), .sel(s1));
endmodule
