// Logisim project fulladderrr.circ as structural Verilog: 5 circuits, main circuit main
module main (
  input  cin,
  input  [3:0] A,
  input  [3:0] B,
  output [3:0] S,
  output cout
);

  wire full1_1_c2, full2_1_c3, fulladder_1_c1;

  fulladder fulladder_1 (.cin(cin), .a0(A[0]), .b0(B[0]), .s0(S[0]), .c1(fulladder_1_c1));
  full1 full1_1 (.c1(fulladder_1_c1), .a1(A[1]), .b1(B[1]), .s1(S[1]), .c2(full1_1_c2));
  full2 full2_1 (.c2(full1_1_c2), .a2(A[2]), .b2(B[2]), .s2(S[2]), .c3(full2_1_c3));
  full3 full3_1 (.c3(full2_1_c3), .a3(A[3]), .b3(B[3]), .s3(S[3]), .cout(cout));
endmodule

module fulladder (
  input  cin,
  input  a0,
  input  b0,
  output s0,
  output c1
);

  wire xor_1_out;

  xor xor_1 (xor_1_out, a0, b0);
  xor xor_2 (s0, cin, xor_1_out);
  Multiplexer #(.enable("false")) multiplexer_1 (.in0(b0), .in1(cin), .out(c1), .sel(xor_1_out));
endmodule

module full1 (
  input  c1,
  input  a1,
  input  b1,
  output s1,
  output c2
);

  wire xor_1_out;

  xor xor_1 (xor_1_out, a1, b1);
  xor xor_2 (s1, c1, xor_1_out);
  Multiplexer #(.enable("false")) multiplexer_1 (.in0(b1), .in1(c1), .out(c2), .sel(xor_1_out));
endmodule

module full2 (
  input  c2,
  input  a2,
  input  b2,
  output s2,
  output c3
);

  wire xor_1_out;

  xor xor_1 (xor_1_out, a2, b2);
  xor xor_2 (s2, c2, xor_1_out);
  Multiplexer #(.enable("false")) multiplexer_1 (.in0(b2), .in1(c2), .out(c3), .sel(xor_1_out));
endmodule

module full3 (
  input  c3,
  input  a3,
  input  b3,
  output s3,
  output cout
);

  wire xor_1_out;

  xor xor_1 (xor_1_out, a3, b3);
  xor xor_2 (s3, c3, xor_1_out);
  Multiplexer #(.enable("false")) multiplexer_1 (.in0(b3), .in1(c3), .out(cout), .sel(xor_1_out));
endmodule
