// Logisim project fullmux.circ as structural Verilog: 20 circuits, main circuit main
module main (
  input  [3:0] A,
  input  [2:0] selecter,
  input  [3:0] B,
  output [7:0] S
);

  wire bar777_1_out_5, bar777_1_out_6, bar777_1_out_7, bar777_1_out_8, bar777_1_out_9, bar777_1_out_10,
       bar777_1_out_11, bar777_2_out_5, bar777_2_out_6, bar777_2_out_7, bar777_2_out_8, bar777_2_out_9,
       bar777_2_out_10, bar777_2_out_11, bar777_3_out_5, bar777_3_out_6, bar777_3_out_7, bar777_3_out_8,
       bar777_3_out_9, bar777_3_out_10, bar777_3_out_11, bar777_4_out_5, bar777_4_out_6, bar777_4_out_7,
       bar777_4_out_8, bar777_4_out_9, bar777_4_out_10, bar777_4_out_11;
  wire [7:0] function0_1_s, function1_1_s, function2_1_s, function3_1_s, function4_1_s, function5_1_s;

  function0 function0_1 (.A(A), .S(function0_1_s));
  function1 function1_1 (.A(A), .B(B), .S(function1_1_s));  // open: in_3, in_4, in_5
  function3 function3_1 (.A(A), .b(B), .S(function3_1_s));
  function2 function2_1 (.A(A), .B(B), .S(function2_1_s));
  function4 function4_1 (.A(A), .S(function4_1_s));  // open: B
  function5 function5_1 (.B(B), .A(A), .S(function5_1_s));
  bar777 bar777_1 (
    .c3(A[3]), .c2(A[2]), .c1(A[1]), .c0(A[0]), .out_5(bar777_1_out_5), .out_6(bar777_1_out_6),
    .out_7(bar777_1_out_7), .out_8(bar777_1_out_8), .out_9(bar777_1_out_9), .out_10(bar777_1_out_10),
    .out_11(bar777_1_out_11));
  bar777 bar777_2 (
    .c3(B[3]), .c2(B[2]), .c1(B[1]), .c0(B[0]), .out_5(bar777_2_out_5), .out_6(bar777_2_out_6),
    .out_7(bar777_2_out_7), .out_8(bar777_2_out_8), .out_9(bar777_2_out_9), .out_10(bar777_2_out_10),
    .out_11(bar777_2_out_11));
  _7_Segment_Display u_7_segment_display_1 (
    .g(bar777_1_out_11), .f(bar777_1_out_10), .a(bar777_1_out_5), .b(bar777_1_out_6), .e(bar777_1_out_9),
    .d(bar777_1_out_8), .c(bar777_1_out_7));  // open: dp
  _7_Segment_Display u_7_segment_display_2 (
    .g(bar777_2_out_11), .f(bar777_2_out_10), .a(bar777_2_out_5), .b(bar777_2_out_6), .e(bar777_2_out_9),
    .d(bar777_2_out_8), .c(bar777_2_out_7));  // open: dp
  Multiplexer #(.enable("false"), .select(3), .width(8)) multiplexer_1 (
    .in0(function0_1_s), .in1(function1_1_s), .in2(function3_1_s), .in3(function2_1_s), .in4(function4_1_s),
    .in5(function5_1_s), .out(S), .sel(selecter));  // open: in6, in7
  LED led_1 (.in(S[0]));
  LED led_2 (.in(S[1]));
  LED led_3 (.in(S[2]));
  LED led_4 (.in(S[3]));
  LED led_5 (.in(S[4]));
  LED led_6 (.in(S[5]));
  LED led_7 (.in(S[6]));
  LED led_8 (.in(S[7]));
  bar777 bar777_3 (
    .c3(S[7]), .c2(S[6]), .c1(S[5]), .c0(S[4]), .out_5(bar777_3_out_5), .out_6(bar777_3_out_6),
    .out_7(bar777_3_out_7), .out_8(bar777_3_out_8), .out_9(bar777_3_out_9), .out_10(bar777_3_out_10),
    .out_11(bar777_3_out_11));
  bar777 bar777_4 (
    .c3(S[3]), .c2(S[2]), .c1(S[1]), .c0(S[0]), .out_5(bar777_4_out_5), .out_6(bar777_4_out_6),
    .out_7(bar777_4_out_7), .out_8(bar777_4_out_8), .out_9(bar777_4_out_9), .out_10(bar777_4_out_10),
    .out_11(bar777_4_out_11));
  _7_Segment_Display u_7_segment_display_3 (
    .g(bar777_3_out_11), .f(bar777_3_out_10), .a(bar777_3_out_5), .b(bar777_3_out_6), .e(bar777_3_out_9),
    .d(bar777_3_out_8), .c(bar777_3_out_7));  // open: dp
  _7_Segment_Display u_7_segment_display_4 (
    .g(bar777_4_out_11), .f(bar777_4_out_10), .a(bar777_4_out_5), .b(bar777_4_out_6), .e(bar777_4_out_9),
    .d(bar777_4_out_8), .c(bar777_4_out_7));  // open: dp
endmodule

module fulladder (
  input  cin,
  input  a0,
  input  b0,
  output s0,
  output c1
);

  wire xor_1_out;

  xor xor_1 (xor_1_out, a0, b0);
  xor xor_2 (s0, cin, xor_1_out);
  Multiplexer #(.enable("false")) multiplexer_1 (.in0(b0), .in1(cin), .out(c1), .sel(xor_1_out));
endmodule

module full1 (
  input  c1,
  input  a1,
  input  b1,
  output s1,
  output c2
);

  wire xor_1_out;

  xor xor_1 (xor_1_out, a1, b1);
  xor xor_2 (s1, c1, xor_1_out);
  Multiplexer #(.enable("false")) multiplexer_1 (.in0(b1), .in1(c1), .out(c2), .sel(xor_1_out));
endmodule

module full2 (
  input  c2,
  input  a2,
  input  b2,
  output s2,
  output c3
);

  wire xor_1_out;

  xor xor_1 (xor_1_out, a2, b2);
  xor xor_2 (s2, c2, xor_1_out);
  Multiplexer #(.enable("false")) multiplexer_1 (.in0(b2), .in1(c2), .out(c3), .sel(xor_1_out));
endmodule

module full3 (
  input  c3,
  input  a3,
  input  b3,
  output s3,
  output cout
);

  wire xor_1_out;

  xor xor_1 (xor_1_out, a3, b3);
  xor xor_2 (s3, c3, xor_1_out);
  Multiplexer #(.enable("false")) multiplexer_1 (.in0(b3), .in1(c3), .out(cout), .sel(xor_1_out));
endmodule

module mainfull (
  input  cin,
  input  [3:0] A,
  input  [3:0] B,
  output s0,
  output s1,
  output s2,
  output s3,
  output cout
);

  wire full1_1_c2, full2_1_c3, fulladder_1_c1;

  fulladder fulladder_1 (.cin(cin), .a0(A[0]), .b0(B[0]), .s0(s0), .c1(fulladder_1_c1));
  full1 full1_1 (.c1(fulladder_1_c1), .a1(A[1]), .b1(B[1]), .s1(s1), .c2(full1_1_c2));
  full2 full2_1 (.c2(full1_1_c2), .a2(A[2]), .b2(B[2]), .s2(s2), .c3(full2_1_c3));
  full3 full3_1 (.c3(full2_1_c3), .a3(A[3]), .b3(B[3]), .s3(s3), .cout(cout));
endmodule

module H0 (
  input  c3,
  input  c2,
  input  c1,
  input  c0,
  output bar0
);

  wire and_1_out, and_2_out, and_3_out, and_4_out, and_5_out, and_6_out, not_1_out, not_2_out, not_3_out,
       not_4_out;

  not not_1 (not_1_out, c3);
  not not_2 (not_2_out, c2);
  not not_3 (not_3_out, c0);
  and and_1 (and_1_out, not_1_out, c1);
  and and_2 (and_2_out, not_2_out, not_3_out);
  and and_3 (and_3_out, c2, c1);
  not not_4 (not_4_out, c1);
  and and_4 (and_4_out, c3, not_3_out);
  and and_5 (and_5_out, not_1_out, c2, c0);
  and and_6 (and_6_out, c3, not_2_out, not_4_out);
  or or_1 (bar0, and_1_out, and_4_out, and_5_out, and_6_out, and_2_out, and_3_out);
endmodule

module H1 (
  input  c3,
  input  c2,
  input  c1,
  input  c0,
  output bar1
);

  wire and_1_out, and_2_out, and_3_out, and_4_out, and_5_out, not_1_out, not_2_out, not_3_out, not_4_out;

  not not_1 (not_1_out, c3);
  not not_2 (not_2_out, c2);
  not not_3 (not_3_out, c1);
  not not_4 (not_4_out, c0);
  and and_1 (and_1_out, not_1_out, not_2_out);
  and and_2 (and_2_out, not_2_out, not_4_out);
  and and_3 (and_3_out, not_1_out, c1, c0);
  and and_4 (and_4_out, not_1_out, not_3_out, not_4_out);
  and and_5 (and_5_out, c3, c0, not_3_out);
  or or_1 (bar1, and_5_out, and_1_out, and_3_out, and_4_out, and_2_out);
endmodule

module H2 (
  input  c3,
  input  c2,
  input  c1,
  input  c0,
  output bar2
);

  wire and_1_out, and_2_out, and_3_out, and_4_out, and_5_out, not_1_out, not_2_out, not_3_out;

  not not_1 (not_1_out, c3);
  not not_2 (not_2_out, c2);
  not not_3 (not_3_out, c1);
  and and_1 (and_1_out, not_1_out, not_3_out);
  and and_2 (and_2_out, not_1_out, c0);
  and and_3 (and_3_out, not_3_out, c0);
  and and_4 (and_4_out, not_1_out, c2);
  and and_5 (and_5_out, c3, not_2_out);
  or or_1 (bar2, and_1_out, and_2_out, and_3_out, and_4_out, and_5_out);
endmodule

module H3 (
  input  c3,
  input  c2,
  input  c1,
  input  c0,
  output bar3
);

  wire and_1_out, and_2_out, and_3_out, and_4_out, and_5_out, not_1_out, not_2_out, not_3_out, not_4_out;

  not not_1 (not_1_out, c2);
  not not_2 (not_2_out, c0);
  not not_3 (not_3_out, c3);
  not not_4 (not_4_out, c1);
  and and_1 (and_1_out, not_1_out, c0, c1);
  and and_2 (and_2_out, not_3_out, not_1_out, not_2_out);
  and and_3 (and_3_out, c2, c0, not_4_out);
  and and_4 (and_4_out, c2, c1, not_2_out);
  and and_5 (and_5_out, c3, not_4_out);
  or or_1 (bar3, and_2_out, and_1_out, and_3_out, and_4_out, and_5_out);
endmodule

module H4 (
  input  c3,
  input  c2,
  input  c1,
  input  c0,
  output bar4
);

  wire and_1_out, and_2_out, and_3_out, and_4_out, not_2_out, not_3_out;

  // NOT_Gate not_1 has open pins: in=c1, out=open
  not not_2 (not_2_out, c0);
  not not_3 (not_3_out, c2);
  and and_1 (and_1_out, not_3_out, not_2_out);
  and and_2 (and_2_out, c1, not_2_out);
  and and_3 (and_3_out, c3, c1);
  and and_4 (and_4_out, c3, c2);
  or or_1 (bar4, and_1_out, and_2_out, and_3_out, and_4_out);
endmodule

module H5 (
  input  c3,
  input  c2,
  input  c1,
  input  c0,
  output bar5
);

  wire and_1_out, and_2_out, and_3_out, and_4_out, and_5_out, not_1_out, not_2_out, not_3_out, not_4_out;

  not not_1 (not_1_out, c3);
  not not_2 (not_2_out, c1);
  not not_3 (not_3_out, c2);
  not not_4 (not_4_out, c0);
  and and_1 (and_1_out, not_2_out, not_4_out);
  and and_2 (and_2_out, not_1_out, c2, not_2_out);
  and and_3 (and_3_out, c2, not_4_out);
  and and_4 (and_4_out, c3, not_3_out);
  and and_5 (and_5_out, c3, c1);
  or or_1 (bar5, and_1_out, and_2_out, and_3_out, and_4_out, and_5_out);
endmodule

module H6 (
  input  c3,
  input  c2,
  input  c1,
  input  c0,
  output bar6
);

  wire and_1_out, and_2_out, and_3_out, and_4_out, and_5_out, not_1_out, not_2_out, not_3_out, not_4_out;

  not not_1 (not_1_out, c2);
  not not_2 (not_2_out, c1);
  not not_3 (not_3_out, c0);
  not not_4 (not_4_out, c3);
  and and_1 (and_1_out, not_1_out, c1);
  and and_2 (and_2_out, c1, not_3_out);
  and and_3 (and_3_out, c3, not_1_out);
  and and_4 (and_4_out, c3, c0);
  and and_5 (and_5_out, not_4_out, not_2_out, c2);
  or or_1 (bar6, and_1_out, and_2_out, and_3_out, and_4_out, and_5_out);
endmodule

module bar777 (
  input  c3,
  input  c2,
  input  c1,
  input  c0,
  output out_5,
  output out_6,
  output out_7,
  output out_8,
  output out_9,
  output out_10,
  output out_11
);

  H0 H0_1 (.c3(c3), .c2(c2), .c1(c1), .c0(c0), .bar0(out_5));
  H1 H1_1 (.c3(c3), .c2(c2), .c1(c1), .c0(c0), .bar1(out_6));
  H2 H2_1 (.c3(c3), .c2(c2), .c1(c1), .c0(c0), .bar2(out_7));
  H3 H3_1 (.c3(c3), .c2(c2), .c1(c1), .c0(c0), .bar3(out_8));
  H4 H4_1 (.c3(c3), .c2(c2), .c1(c1), .c0(c0), .bar4(out_9));
  H5 H5_1 (.c3(c3), .c2(c2), .c1(c1), .c0(c0), .bar5(out_10));
  H6 H6_1 (.c3(c3), .c2(c2), .c1(c1), .c0(c0), .bar6(out_11));
endmodule

module function0 (
  input  [3:0] A,
  output [7:0] S
);

  mainfull mainfull_1 (.cin(1'b1), .A(A), .s0(S[0]), .s1(S[1]), .s2(S[2]), .s3(S[3]), .cout(S[4]));  // open: B
  not not_1 (S[7], 1'b1);

  assign S[6:5] = {2{S[7]}};
endmodule

module function1 (
  input  [3:0] A,
  input  [3:0] B,
  input  in_3,
  input  in_4,
  input  in_5,
  output [7:0] S
);

  mainfull mainfull_1 (.A(A), .B(B), .s0(S[0]), .s1(S[1]), .s2(S[2]), .s3(S[3]), .cout(S[4]));  // open: cin

  assign S[7:5] = {in_5, in_4, in_3};
endmodule

module function2 (
  input  [3:0] A,
  input  [3:0] B,
  output [7:0] S
);

  assign S[7:4] = A | B;  // OR_Gate or_1, 4 bits wide
  assign S[3:0] = A ^ B;  // XOR_Gate xor_1, 4 bits wide
endmodule

module function4 (
  input  [3:0] A,
  input  [3:0] B,
  output [7:0] S
);

  wire or_1_out;

  or or_1 (or_1_out, A[0], A[1], A[2], A[3], B[0], B[1], B[2], B[3]);
  mainfull mainfull_1 (.cin(or_1_out), .s0(S[0]), .s1(S[1]), .s2(S[2]), .s3(S[3]), .cout(S[4]));  // open: A, B
  not not_1 (S[7], 1'b1);

  assign S[6:5] = {2{S[7]}};
endmodule

module function5 (
  input  [3:0] B,
  input  [3:0] A,
  output [7:0] S
);


  assign S = {A, B};
endmodule

module function3 (
  input  [3:0] A,
  input  [3:0] b,
  output [7:0] S
);

  not not_1 (S[7], 1'b1);
  Adder #(.width(4)) adder_1 (.a(A), .b(b), .out(S[3:0]), .cout(S[4]));  // open: cin

  assign S[6:5] = {2{S[7]}};
endmodule
