// Logisim project part1.circ as structural Verilog: 1 circuit, main circuit main
module main (
  input  [6:0] ad,
  input  [2:0] selector,
  output s
);

  Multiplexer #(.enable("false"), .select(3)) multiplexer_1 (
    .in0(ad[0]), .in1(ad[1]), .in2(ad[2]), .in3(ad[3]), .in4(ad[4]), .in5(ad[5]), .in6(ad[6]), .out(s),
    .sel(selector));  // open: in7
endmodule
