// Logisim project part1.circ as structural Verilog: 3 circuits, main circuit main
module main (
  input  D,
  input  Clk,
  output Q
);

  wire d1_1_qa;

  d1 d1_1 (.D(D), .Clk(Clk), .Qa(d1_1_qa));  // open: Qb
  d2 d2_1 (.D(d1_1_qa), .Clk(Clk), .Qa(Q));  // open: Qb
endmodule

module d1 (
  input  D,
  input  Clk,
  output Qa,
  output Qb
);

  wire nand_1_out, nand_2_out, not_1_out;

  not not_1 (not_1_out, D);
  nand nand_1 (nand_1_out, D, Clk);
  nand nand_2 (nand_2_out, Clk, not_1_out);
  nand nand_3 (Qa, nand_1_out, Qb);
  nand nand_4 (Qb, Qa, nand_2_out);
endmodule

module d2 (
  input  D,
  input  Clk,
  output Qa,
  output Qb
);

  wire nand_1_out, nand_2_out, not_1_out;

  not not_1 (not_1_out, D);
  nand nand_1 (nand_1_out, D, Clk);
  nand nand_2 (nand_2_out, Clk, not_1_out);
  nand nand_3 (Qa, nand_1_out, Qb);
  nand nand_4 (Qb, Qa, nand_2_out);
endmodule
