// Logisim project part3.circ as structural Verilog: 4 circuits, main circuit main
module main (
  input  [7:0] load_val,
  input  Asrr,
  input  shift,
  input  reset,
  input  load_n,
  input  clk,
  output [7:0] out_7
);

  wire asr_1_inn;

  asr asr_1 (.A(load_val), .ASrr(Asrr), .inn(asr_1_inn));
  shitfer shitfer_1 (
    .load_val(load_val[7]), .inn(asr_1_inn), .shift(shift), .reset(reset), .load_n(load_n), .clk(clk),
    .O(out_7[7]));
  shitfer shitfer_2 (
    .load_val(load_val[6]), .inn(out_7[7]), .shift(shift), .reset(reset), .load_n(load_n), .clk(clk),
    .O(out_7[6]));
  shitfer shitfer_3 (
    .load_val(load_val[5]), .inn(out_7[6]), .shift(shift), .reset(reset), .load_n(load_n), .clk(clk),
    .O(out_7[5]));
  shitfer shitfer_4 (
    .load_val(load_val[4]), .inn(out_7[5]), .shift(shift), .reset(reset), .load_n(load_n), .clk(clk),
    .O(out_7[4]));
  shitfer shitfer_5 (
    .load_val(load_val[3]), .inn(out_7[4]), .shift(shift), .reset(reset), .load_n(load_n), .clk(clk),
    .O(out_7[3]));
  shitfer shitfer_6 (
    .load_val(load_val[2]), .inn(out_7[3]), .shift(shift), .reset(reset), .load_n(load_n), .clk(clk),
    .O(out_7[2]));
  shitfer shitfer_7 (
    .load_val(load_val[1]), .inn(out_7[2]), .shift(shift), .reset(reset), .load_n(load_n), .clk(clk),
    .O(out_7[1]));
  shitfer shitfer_8 (
    .load_val(load_val[0]), .inn(out_7[1]), .shift(shift), .reset(reset), .load_n(load_n), .clk(clk),
    .O(out_7[0]));
endmodule

module shitfer (
  input  load_val,
  input  inn,
  input  shift,
  input  reset,
  input  load_n,
  input  clk,
  output O
);

  wire mux2to1_1_m, mux2to1_2_m;

  mux2to1 mux2to1_1 (.x(O), .y(inn), .s(shift), .m(mux2to1_1_m));
  mux2to1 mux2to1_2 (.x(load_val), .y(mux2to1_1_m), .s(load_n), .m(mux2to1_2_m));
  D_Flip_Flop d_ff_1 (.D(mux2to1_2_m), .clk(clk), .Q(O), .reset(reset));  // open: Qn, preset
endmodule

module asr (
  input  [7:0] A,
  input  ASrr,
  output inn
);

  wire not_1_out;

  not not_1 (not_1_out, 1'b1);
  mux2to1 mux2to1_1 (.x(not_1_out), .y(A[7]), .s(ASrr), .m(inn));
endmodule

module mux2to1 (
  input  x,
  input  y,
  input  s,
  output m
);

  Multiplexer #(.enable("false")) multiplexer_1 (.in0(x), .in1(y), .out(m), .sel(s));
endmodule
