// Logisim project part1.circ as structural Verilog: 9 circuits, main circuit main
module main (
  input  Enable,
  input  Clear_b,
  output [7:0] Q
);

  wire and_1_out, and_2_out, and_3_out, and_4_out, and_5_out, and_6_out, and_7_out, bar_1_out_5, bar_1_out_6,
       bar_1_out_7, bar_1_out_8, bar_1_out_9, bar_1_out_10, bar_1_out_11, bar_2_out_5, bar_2_out_6,
       bar_2_out_7, bar_2_out_8, bar_2_out_9, bar_2_out_10, bar_2_out_11, clock_1_out, not_1_out;

  Clock clock_1 (.out(clock_1_out));
  T_Flip_Flop t_ff_1 (.T(Enable), .clk(clock_1_out), .Q(Q[0]));  // open: Qn, reset, preset
  and and_1 (and_1_out, Enable, Q[0]);
  not not_1 (not_1_out, Clear_b);
  T_Flip_Flop t_ff_2 (.T(and_1_out), .clk(clock_1_out), .Q(Q[1]), .reset(not_1_out));  // open: Qn, preset
  and and_2 (and_2_out, and_1_out, Q[1]);
  T_Flip_Flop t_ff_3 (.T(and_2_out), .clk(clock_1_out), .Q(Q[2]), .reset(not_1_out));  // open: Qn, preset
  and and_3 (and_3_out, and_2_out, Q[2]);
  T_Flip_Flop t_ff_4 (.T(and_3_out), .clk(clock_1_out), .Q(Q[3]), .reset(not_1_out));  // open: Qn, preset
  and and_4 (and_4_out, and_3_out, Q[3]);
  T_Flip_Flop t_ff_5 (.T(and_4_out), .clk(clock_1_out), .Q(Q[4]), .reset(not_1_out));  // open: Qn, preset
  and and_5 (and_5_out, and_4_out, Q[4]);
  T_Flip_Flop t_ff_6 (.T(and_5_out), .clk(clock_1_out), .Q(Q[5]), .reset(not_1_out));  // open: Qn, preset
  and and_6 (and_6_out, and_5_out, Q[5]);
  T_Flip_Flop t_ff_7 (.T(and_6_out), .clk(clock_1_out), .Q(Q[6]), .reset(not_1_out));  // open: Qn, preset
  and and_7 (and_7_out, and_6_out, Q[6]);
  T_Flip_Flop t_ff_8 (.T(and_7_out), .clk(clock_1_out), .Q(Q[7]), .reset(not_1_out));  // open: Qn, preset
  bar bar_1 (
    .c3(Q[3]), .c2(Q[2]), .c1(Q[1]), .c0(Q[0]), .out_5(bar_1_out_5), .out_6(bar_1_out_6),
    .out_7(bar_1_out_7), .out_8(bar_1_out_8), .out_9(bar_1_out_9), .out_10(bar_1_out_10),
    .out_11(bar_1_out_11));
  bar bar_2 (
    .c3(Q[7]), .c2(Q[6]), .c1(Q[5]), .c0(Q[4]), .out_5(bar_2_out_5), .out_6(bar_2_out_6),
    .out_7(bar_2_out_7), .out_8(bar_2_out_8), .out_9(bar_2_out_9), .out_10(bar_2_out_10),
    .out_11(bar_2_out_11));
  _7_Segment_Display u_7_segment_display_1 (
    .g(bar_1_out_11), .f(bar_1_out_10), .a(bar_1_out_5), .b(bar_1_out_6), .e(bar_1_out_9), .d(bar_1_out_8),
    .c(bar_1_out_7));  // open: dp
  _7_Segment_Display u_7_segment_display_2 (
    .g(bar_2_out_11), .f(bar_2_out_10), .a(bar_2_out_5), .b(bar_2_out_6), .e(bar_2_out_9), .d(bar_2_out_8),
    .c(bar_2_out_7));  // open: dp
endmodule

module H0 (
  input  c3,
  input  c2,
  input  c1,
  input  c0,
  output bar0
);

  wire and_1_out, and_2_out, and_3_out, and_4_out, and_5_out, and_6_out, not_1_out, not_2_out, not_3_out,
       not_4_out;

  not not_1 (not_1_out, c3);
  not not_2 (not_2_out, c2);
  not not_3 (not_3_out, c0);
  and and_1 (and_1_out, not_1_out, c1);
  and and_2 (and_2_out, not_2_out, not_3_out);
  and and_3 (and_3_out, c2, c1);
  not not_4 (not_4_out, c1);
  and and_4 (and_4_out, c3, not_3_out);
  and and_5 (and_5_out, not_1_out, c2, c0);
  and and_6 (and_6_out, c3, not_2_out, not_4_out);
  or or_1 (bar0, and_1_out, and_4_out, and_5_out, and_6_out, and_2_out, and_3_out);
endmodule

module H1 (
  input  c3,
  input  c2,
  input  c1,
  input  c0,
  output bar1
);

  wire and_1_out, and_2_out, and_3_out, and_4_out, and_5_out, not_1_out, not_2_out, not_3_out, not_4_out;

  not not_1 (not_1_out, c3);
  not not_2 (not_2_out, c2);
  not not_3 (not_3_out, c1);
  not not_4 (not_4_out, c0);
  and and_1 (and_1_out, not_1_out, not_2_out);
  and and_2 (and_2_out, not_2_out, not_4_out);
  and and_3 (and_3_out, not_1_out, c1, c0);
  and and_4 (and_4_out, not_1_out, not_3_out, not_4_out);
  and and_5 (and_5_out, c3, c0, not_3_out);
  or or_1 (bar1, and_5_out, and_1_out, and_3_out, and_4_out, and_2_out);
endmodule

module H2 (
  input  c3,
  input  c2,
  input  c1,
  input  c0,
  output bar2
);

  wire and_1_out, and_2_out, and_3_out, and_4_out, and_5_out, not_1_out, not_2_out, not_3_out;

  not not_1 (not_1_out, c3);
  not not_2 (not_2_out, c2);
  not not_3 (not_3_out, c1);
  and and_1 (and_1_out, not_1_out, not_3_out);
  and and_2 (and_2_out, not_1_out, c0);
  and and_3 (and_3_out, not_3_out, c0);
  and and_4 (and_4_out, not_1_out, c2);
  and and_5 (and_5_out, c3, not_2_out);
  or or_1 (bar2, and_1_out, and_2_out, and_3_out, and_4_out, and_5_out);
endmodule

module H3 (
  input  c3,
  input  c2,
  input  c1,
  input  c0,
  output bar3
);

  wire and_1_out, and_2_out, and_3_out, and_4_out, and_5_out, not_1_out, not_2_out, not_3_out, not_4_out;

  not not_1 (not_1_out, c2);
  not not_2 (not_2_out, c0);
  not not_3 (not_3_out, c3);
  not not_4 (not_4_out, c1);
  and and_1 (and_1_out, not_1_out, c0, c1);
  and and_2 (and_2_out, not_3_out, not_1_out, not_2_out);
  and and_3 (and_3_out, c2, c0, not_4_out);
  and and_4 (and_4_out, c2, c1, not_2_out);
  and and_5 (and_5_out, c3, not_4_out);
  or or_1 (bar3, and_2_out, and_1_out, and_3_out, and_4_out, and_5_out);
endmodule

module H4 (
  input  c3,
  input  c2,
  input  c1,
  input  c0,
  output bar4
);

  wire and_1_out, and_2_out, and_3_out, and_4_out, not_2_out, not_3_out;

  // NOT_Gate not_1 has open pins: in=c1, out=open
  not not_2 (not_2_out, c0);
  not not_3 (not_3_out, c2);
  and and_1 (and_1_out, not_3_out, not_2_out);
  and and_2 (and_2_out, c1, not_2_out);
  and and_3 (and_3_out, c3, c1);
  and and_4 (and_4_out, c3, c2);
  or or_1 (bar4, and_1_out, and_2_out, and_3_out, and_4_out);
endmodule

module H5 (
  input  c3,
  input  c2,
  input  c1,
  input  c0,
  output bar5
);

  wire and_1_out, and_2_out, and_3_out, and_4_out, and_5_out, not_1_out, not_2_out, not_3_out, not_4_out;

  not not_1 (not_1_out, c3);
  not not_2 (not_2_out, c1);
  not not_3 (not_3_out, c2);
  not not_4 (not_4_out, c0);
  and and_1 (and_1_out, not_2_out, not_4_out);
  and and_2 (and_2_out, not_1_out, c2, not_2_out);
  and and_3 (and_3_out, c2, not_4_out);
  and and_4 (and_4_out, c3, not_3_out);
  and and_5 (and_5_out, c3, c1);
  or or_1 (bar5, and_1_out, and_2_out, and_3_out, and_4_out, and_5_out);
endmodule

module H6 (
  input  c3,
  input  c2,
  input  c1,
  input  c0,
  output bar6
);

  wire and_1_out, and_2_out, and_3_out, and_4_out, and_5_out, not_1_out, not_2_out, not_3_out, not_4_out;

  not not_1 (not_1_out, c2);
  not not_2 (not_2_out, c1);
  not not_3 (not_3_out, c0);
  not not_4 (not_4_out, c3);
  and and_1 (and_1_out, not_1_out, c1);
  and and_2 (and_2_out, c1, not_3_out);
  and and_3 (and_3_out, c3, not_1_out);
  and and_4 (and_4_out, c3, c0);
  and and_5 (and_5_out, not_4_out, not_2_out, c2);
  or or_1 (bar6, and_1_out, and_2_out, and_3_out, and_4_out, and_5_out);
endmodule

module bar (
  input  c3,
  input  c2,
  input  c1,
  input  c0,
  output out_5,
  output out_6,
  output out_7,
  output out_8,
  output out_9,
  output out_10,
  output out_11
);

  H0 h0_1 (.c3(c3), .c2(c2), .c1(c1), .c0(c0), .bar0(out_5));
  H1 h1_1 (.c3(c3), .c2(c2), .c1(c1), .c0(c0), .bar1(out_6));
  H2 h2_1 (.c3(c3), .c2(c2), .c1(c1), .c0(c0), .bar2(out_7));
  H3 h3_1 (.c3(c3), .c2(c2), .c1(c1), .c0(c0), .bar3(out_8));
  H4 h4_1 (.c3(c3), .c2(c2), .c1(c1), .c0(c0), .bar4(out_9));
  H5 h5_1 (.c3(c3), .c2(c2), .c1(c1), .c0(c0), .bar5(out_10));
  H6 h6_1 (.c3(c3), .c2(c2), .c1(c1), .c0(c0), .bar6(out_11));
endmodule
