// Logisim project part2.circ as structural Verilog: 10 circuits, main circuit Ratedivider
module Ratedivider (
  input  clear,
  input  enable,
  input  clockk,
  input  [1:0] Sw,
  output Counter_out
);

  wire and_1_out, and_2_out, and_3_out, and_4_out, not_1_out, not_2_out, not_3_out, not_4_out, not_5_out,
       not_6_out, not_7_out, not_8_out, not_9_out, not_10_out, or_1_out;
  wire [5:0] counter_1_q;

  not not_1 (not_1_out, enable);
  or or_1 (or_1_out, Counter_out, not_1_out);
  Counter #(.max('h3f), .width(6)) counter_1 (
    .clr(clear), .load(or_1_out), .up(1'b1), .clk(clockk), .D({6{1'b0}}), .Q(counter_1_q));  // open: count, carry
  not not_2 (not_2_out, counter_1_q[0]);
  not not_3 (not_3_out, counter_1_q[1]);
  not not_4 (not_4_out, counter_1_q[2]);
  and and_1 (and_1_out, not_2_out, not_3_out, not_4_out, not_5_out, not_6_out, not_7_out);
  not not_5 (not_5_out, counter_1_q[3]);
  not not_6 (not_6_out, counter_1_q[4]);
  not not_7 (not_7_out, counter_1_q[5]);
  and and_2 (and_2_out, counter_1_q[0], counter_1_q[1], counter_1_q[2], counter_1_q[3], not_8_out, not_9_out);
  not not_8 (not_8_out, counter_1_q[4]);
  not not_9 (not_9_out, counter_1_q[5]);
  and and_3 (and_3_out, counter_1_q[0], counter_1_q[1], counter_1_q[2], counter_1_q[3], counter_1_q[4], not_10_out);
  not not_10 (not_10_out, counter_1_q[5]);
  and and_4 (and_4_out, counter_1_q[0], counter_1_q[1], counter_1_q[2], counter_1_q[3], counter_1_q[4], counter_1_q[5]);
  Multiplexer #(.enable("false"), .select(2)) multiplexer_1 (
    .in0(and_1_out), .in1(and_2_out), .in2(and_3_out), .in3(and_4_out), .out(Counter_out), .sel(Sw));
endmodule

module DisplayCounter (
  input  clear,
  input  in_2,
  input  [1:0] SW,
  output counter_out
);

  wire clock_1_out, main_1_out_5, main_1_out_6, main_1_out_7, main_1_out_8, main_1_out_9, main_1_out_10,
       main_1_out_11, not_1_out, or_1_out, ratedivider_1_counter_out;
  wire [3:0] counter_1_q, multiplexer_1_out, not_2_out;

  Clock clock_1 (.out(clock_1_out));
  not not_1 (not_1_out, ratedivider_1_counter_out);
  Ratedivider ratedivider_1 (
    .clear(clear), .enable(in_2), .clockk(clock_1_out), .Sw(SW), .Counter_out(ratedivider_1_counter_out));
  or or_1 (or_1_out, counter_out, not_1_out);
  Multiplexer #(.enable("false"), .width(4)) multiplexer_1 (
    .in0(counter_1_q), .in1(not_2_out), .out(multiplexer_1_out), .sel(counter_out));
  Counter #(.max('hf), .width(4)) counter_1 (
    .clr(clear), .load(or_1_out), .up(1'b1), .clk(clock_1_out), .D(multiplexer_1_out), .Q(counter_1_q));  // open: count, carry
  assign not_2_out = ~4'b1111;  // NOT_Gate not_2, 4 bits wide
  Hex_Digit_Display hex_digit_display_1 (.value(counter_1_q));  // open: dp
  and and_1 (counter_out, counter_1_q[0], counter_1_q[1], counter_1_q[2], counter_1_q[3]);
  main main_1 (
    .c3(counter_1_q[3]), .c2(counter_1_q[2]), .c1(counter_1_q[1]), .c0(counter_1_q[0]), .out_5(main_1_out_5),
    .out_6(main_1_out_6), .out_7(main_1_out_7), .out_8(main_1_out_8), .out_9(main_1_out_9),
    .out_10(main_1_out_10), .out_11(main_1_out_11));
  _7_Segment_Display u_7_segment_display_1 (
    .g(main_1_out_11), .f(main_1_out_10), .a(main_1_out_5), .b(main_1_out_6), .e(main_1_out_9),
    .d(main_1_out_8), .c(main_1_out_7));  // open: dp
endmodule

module main (
  input  c3,
  input  c2,
  input  c1,
  input  c0,
  output out_5,
  output out_6,
  output out_7,
  output out_8,
  output out_9,
  output out_10,
  output out_11
);

  H0 H0_1 (.c3(c3), .c2(c2), .c1(c1), .c0(c0), .bar0(out_5));
  H1 H1_1 (.c3(c3), .c2(c2), .c1(c1), .c0(c0), .bar1(out_6));
  H2 H2_1 (.c3(c3), .c2(c2), .c1(c1), .c0(c0), .bar2(out_7));
  H3 H3_1 (.c3(c3), .c2(c2), .c1(c1), .c0(c0), .bar3(out_8));
  H4 H4_1 (.c3(c3), .c2(c2), .c1(c1), .c0(c0), .bar4(out_9));
  H5 H5_1 (.c3(c3), .c2(c2), .c1(c1), .c0(c0), .bar5(out_10));
  H6 H6_1 (.c3(c3), .c2(c2), .c1(c1), .c0(c0), .bar6(out_11));
endmodule

module H0 (
  input  c3,
  input  c2,
  input  c1,
  input  c0,
  output bar0
);

  wire and_1_out, and_2_out, and_3_out, and_4_out, and_5_out, and_6_out, not_1_out, not_2_out, not_3_out,
       not_4_out;

  not not_1 (not_1_out, c3);
  not not_2 (not_2_out, c2);
  not not_3 (not_3_out, c0);
  and and_1 (and_1_out, not_1_out, c1);
  and and_2 (and_2_out, not_2_out, not_3_out);
  and and_3 (and_3_out, c2, c1);
  not not_4 (not_4_out, c1);
  and and_4 (and_4_out, c3, not_3_out);
  and and_5 (and_5_out, not_1_out, c2, c0);
  and and_6 (and_6_out, c3, not_2_out, not_4_out);
  or or_1 (bar0, and_1_out, and_4_out, and_5_out, and_6_out, and_2_out, and_3_out);
endmodule

module H1 (
  input  c3,
  input  c2,
  input  c1,
  input  c0,
  output bar1
);

  wire and_1_out, and_2_out, and_3_out, and_4_out, and_5_out, not_1_out, not_2_out, not_3_out, not_4_out;

  not not_1 (not_1_out, c3);
  not not_2 (not_2_out, c2);
  not not_3 (not_3_out, c1);
  not not_4 (not_4_out, c0);
  and and_1 (and_1_out, not_1_out, not_2_out);
  and and_2 (and_2_out, not_2_out, not_4_out);
  and and_3 (and_3_out, not_1_out, c1, c0);
  and and_4 (and_4_out, not_1_out, not_3_out, not_4_out);
  and and_5 (and_5_out, c3, c0, not_3_out);
  or or_1 (bar1, and_5_out, and_1_out, and_3_out, and_4_out, and_2_out);
endmodule

module H2 (
  input  c3,
  input  c2,
  input  c1,
  input  c0,
  output bar2
);

  wire and_1_out, and_2_out, and_3_out, and_4_out, and_5_out, not_1_out, not_2_out, not_3_out;

  not not_1 (not_1_out, c3);
  not not_2 (not_2_out, c2);
  not not_3 (not_3_out, c1);
  and and_1 (and_1_out, not_1_out, not_3_out);
  and and_2 (and_2_out, not_1_out, c0);
  and and_3 (and_3_out, not_3_out, c0);
  and and_4 (and_4_out, not_1_out, c2);
  and and_5 (and_5_out, c3, not_2_out);
  or or_1 (bar2, and_1_out, and_2_out, and_3_out, and_4_out, and_5_out);
endmodule

module H3 (
  input  c3,
  input  c2,
  input  c1,
  input  c0,
  output bar3
);

  wire and_1_out, and_2_out, and_3_out, and_4_out, and_5_out, not_1_out, not_2_out, not_3_out, not_4_out;

  not not_1 (not_1_out, c2);
  not not_2 (not_2_out, c0);
  not not_3 (not_3_out, c3);
  not not_4 (not_4_out, c1);
  and and_1 (and_1_out, not_1_out, c0, c1);
  and and_2 (and_2_out, not_3_out, not_1_out, not_2_out);
  and and_3 (and_3_out, c2, c0, not_4_out);
  and and_4 (and_4_out, c2, c1, not_2_out);
  and and_5 (and_5_out, c3, not_4_out);
  or or_1 (bar3, and_2_out, and_1_out, and_3_out, and_4_out, and_5_out);
endmodule

module H4 (
  input  c3,
  input  c2,
  input  c1,
  input  c0,
  output bar4
);

  wire and_1_out, and_2_out, and_3_out, and_4_out, not_2_out, not_3_out;

  // NOT_Gate not_1 has open pins: in=c1, out=open
  not not_2 (not_2_out, c0);
  not not_3 (not_3_out, c2);
  and and_1 (and_1_out, not_3_out, not_2_out);
  and and_2 (and_2_out, c1, not_2_out);
  and and_3 (and_3_out, c3, c1);
  and and_4 (and_4_out, c3, c2);
  or or_1 (bar4, and_1_out, and_2_out, and_3_out, and_4_out);
endmodule

module H5 (
  input  c3,
  input  c2,
  input  c1,
  input  c0,
  output bar5
);

  wire and_1_out, and_2_out, and_3_out, and_4_out, and_5_out, not_1_out, not_2_out, not_3_out, not_4_out;

  not not_1 (not_1_out, c3);
  not not_2 (not_2_out, c1);
  not not_3 (not_3_out, c2);
  not not_4 (not_4_out, c0);
  and and_1 (and_1_out, not_2_out, not_4_out);
  and and_2 (and_2_out, not_1_out, c2, not_2_out);
  and and_3 (and_3_out, c2, not_4_out);
  and and_4 (and_4_out, c3, not_3_out);
  and and_5 (and_5_out, c3, c1);
  or or_1 (bar5, and_1_out, and_2_out, and_3_out, and_4_out, and_5_out);
endmodule

module H6 (
  input  c3,
  input  c2,
  input  c1,
  input  c0,
  output bar6
);

  wire and_1_out, and_2_out, and_3_out, and_4_out, and_5_out, not_1_out, not_2_out, not_3_out, not_4_out;

  not not_1 (not_1_out, c2);
  not not_2 (not_2_out, c1);
  not not_3 (not_3_out, c0);
  not not_4 (not_4_out, c3);
  and and_1 (and_1_out, not_1_out, c1);
  and and_2 (and_2_out, c1, not_3_out);
  and and_3 (and_3_out, c3, not_1_out);
  and and_4 (and_4_out, c3, c0);
  and and_5 (and_5_out, not_4_out, not_2_out, c2);
  or or_1 (bar6, and_1_out, and_2_out, and_3_out, and_4_out, and_5_out);
endmodule
