// Logisim project part3.circ as structural Verilog: 4 circuits, main circuit main
module main (
  input  Key0,
  input  Key1,
  input  [2:0] SW
);

  wire clock_1_out, ratedivider_1_counter_out, undriven;

  Clock clock_1 (.out(clock_1_out));
  ratedivider ratedivider_1 (
    .clear(Key0), .enable(Key1), .clockk(clock_1_out), .Counter_out(ratedivider_1_counter_out));
  shift shift_1 (.key0(undriven));  // open: SW
  LED led_1 (.in(undriven));
endmodule

module LUT (
  input  [2:0] SW,
  output [13:0] O
);

  wire [9:9] not_2_out;
  wire [10:10] not_6_out, not_7_out, not_8_out;
  wire [12:12] not_1_out, not_3_out, not_4_out, not_5_out;

  not not_1 (not_1_out[12], 1'b1);
  not not_2 (not_2_out[9], 1'b1);
  not not_3 (not_3_out[12], 1'b1);
  not not_4 (not_4_out[12], 1'b1);
  not not_5 (not_5_out[12], 1'b1);
  not not_6 (not_6_out[10], 1'b1);
  not not_7 (not_7_out[10], 1'b1);
  not not_8 (not_8_out[10], 1'b1);
  Multiplexer #(.enable("false"), .select(3), .width(14)) multiplexer_1 (
    .in0({1'b1, not_1_out[12], 1'b1, not_1_out[12], 1'b1, not_1_out[12], 1'b1, {7{not_1_out[12]}}}),
    .in1({4'b1111, {10{not_2_out[9]}}}),
    .in2({1'b1, not_3_out[12], 1'b1, not_3_out[12], 3'b111, {7{not_3_out[12]}}}),
    .in3({1'b1, not_4_out[12], 1'b1, not_4_out[12], 1'b1, not_4_out[12], 3'b111, {5{not_4_out[12]}}}),
    .in4({1'b1, not_5_out[12], 3'b111, not_5_out[12], 3'b111, {5{not_5_out[12]}}}),
    .in5({3'b111, not_6_out[10], 1'b1, not_6_out[10], 1'b1, not_6_out[10], 3'b111, {3{not_6_out[10]}}}),
    .in6({3'b111, not_7_out[10], 1'b1, not_7_out[10], 3'b111, not_7_out[10], 3'b111, not_7_out[10]}),
    .in7({3'b111, not_8_out[10], 3'b111, not_8_out[10], 1'b1, not_8_out[10], 1'b1, {3{not_8_out[10]}}}),
    .out(O), .sel(SW));
endmodule

module shift (
  input  key0,
  input  [2:0] SW
);

  wire clock_1_out, key1_out, not_1_out, ratedivider_1_counter_out, undriven;
  wire [13:0] lut_1_o;

  Clock clock_1 (.out(clock_1_out));
  Button key1 (.out(key1_out));
  not not_1 (not_1_out, key1_out);
  ratedivider ratedivider_1 (
    .clear(key0), .enable(not_1_out), .clockk(clock_1_out), .Counter_out(ratedivider_1_counter_out));
  LUT lut_1 (.SW(SW), .O(lut_1_o));
  // Shift_Register #(.length(14)) shift_register_1: pin names not known; wires that end beside it: key0, key1_out, ratedivider_1_counter_out, clock_1_out, 1'b0, lut_1_o[0], lut_1_o[1], lut_1_o[2], lut_1_o[3], lut_1_o[4], lut_1_o[5], lut_1_o[6], lut_1_o[7], lut_1_o[8], lut_1_o[9], lut_1_o[10], lut_1_o[11]
  LED led_1 (.in(undriven));
endmodule

module ratedivider (
  input  clear,
  input  enable,
  input  clockk,
  output Counter_out
);

  wire not_1_out, not_3_out, or_1_out;
  wire [5:0] counter_1_q;
  wire [5:5] not_2_out;

  not not_1 (not_1_out, enable);
  not not_2 (not_2_out[5], 1'b1);
  or or_1 (or_1_out, Counter_out, not_1_out);
  Counter #(.max('h3f), .width(6)) counter_1 (
    .clr(clear), .load(or_1_out), .up(not_3_out), .clk(clockk),
    .D({{2{not_2_out[5]}}, 1'b1, {3{not_2_out[5]}}}), .Q(counter_1_q));  // open: count, carry
  not not_3 (not_3_out, 1'b1);
  and and_1 (Counter_out, counter_1_q[0], counter_1_q[1], counter_1_q[2], counter_1_q[3], counter_1_q[4], counter_1_q[5]);
endmodule
