// Logisim project lab6_starter.circ as structural Verilog
module part_1_state_table (
  input  [2:0] curr_state,
  input  w,
  output [2:0] next_state
);

  wire [2:0] a_1_o, b_1_o, c_1_o, d_1_o, e_1_o, f_1_o, g_1_o;

  A a_1 (.W(w), .O(a_1_o));
  B b_1 (.W(w), .O(b_1_o));
  G g_1 (.W(w), .O(g_1_o));
  C c_1 (.W(w), .O(c_1_o));
  D d_1 (.W(w), .O(d_1_o));
  E e_1 (.W(w), .O(e_1_o));
  F f_1 (.W(w), .O(f_1_o));
  Multiplexer #(.enable("false"), .select(3), .width(3)) multiplexer_1 (
    .in0(a_1_o), .in1(b_1_o), .in2(g_1_o), .in3(c_1_o), .in5(f_1_o), .in6(e_1_o), .in7(d_1_o),
    .out(next_state), .sel(curr_state));  // open: in4

  // Notes on the sheet:
  //   This is the state table, refer to the state diagram. To be completed by you. 
endmodule

module part_1_FSM (
  input  W,
  input  Enable,
  input  Reset,
  output z
);

  wire Clk_out;
  wire [2:0] state_q, state_table_next_state;

  part_1_state_table state_table (.curr_state(state_q), .w(W), .next_state(state_table_next_state));
  Register #(.width(3)) state (.D(state_table_next_state), .en(Enable), .clk(Clk_out), .Q(state_q), .clr(Reset));
  Clock Clk (.out(Clk_out));
  part1_output part1_output_1 (.Q(state_q), .O(z));

  // Notes on the sheet:
  //   your state table
  //   state register
  //   output logic (to be completed by you)
endmodule

module part_2_datapath (
  input  ld_alu_out,
  input  [7:0] data_in,
  input  clk,
  input  ld_c,
  input  ld_x,
  input  ld_a,
  input  ld_b,
  input  Reset,
  input  [1:0] alu_select_a,
  input  [1:0] alu_select_b,
  input  alu_op,
  input  ld_r,
  output [7:0] R_B_val,
  output [7:0] R_A_val,
  output [7:0] R_X_val,
  output [7:0] R_C_val,
  output [7:0] data_result
);

  wire [7:0] multiplexer_1_out, multiplexer_2_out, multiplexer_3_out, multiplexer_4_out, part_2_alu_1_alu_out;

  Register R_C (.D(data_in), .en(ld_c), .clk(clk), .Q(R_C_val), .clr(Reset));
  Register R_X (.D(data_in), .en(ld_x), .clk(clk), .Q(R_X_val), .clr(Reset));
  Multiplexer #(.enable("false"), .select(2), .width(8)) multiplexer_1 (
    .in0(R_A_val), .in1(R_B_val), .in2(R_C_val), .in3(R_X_val), .out(multiplexer_1_out), .sel(alu_select_a));
  Multiplexer #(.enable("false"), .width(8)) multiplexer_2 (
    .in0(data_in), .in1(part_2_alu_1_alu_out), .out(multiplexer_2_out), .sel(ld_alu_out));
  Register R_A (.D(multiplexer_2_out), .en(ld_a), .clk(clk), .Q(R_A_val), .clr(Reset));
  Multiplexer #(.enable("false"), .select(2), .width(8)) multiplexer_3 (
    .in0(R_A_val), .in1(R_B_val), .in2(R_C_val), .in3(R_X_val), .out(multiplexer_3_out), .sel(alu_select_b));
  part_2_ALU part_2_alu_1 (
    .input_1(multiplexer_1_out), .input_2(multiplexer_3_out), .ALU_op(alu_op), .ALU_out(part_2_alu_1_alu_out));
  Multiplexer #(.enable("false"), .width(8)) multiplexer_4 (
    .in0(data_in), .in1(part_2_alu_1_alu_out), .out(multiplexer_4_out), .sel(ld_alu_out));
  Register R_B (.D(multiplexer_4_out), .en(ld_b), .clk(clk), .Q(R_B_val), .clr(Reset));
  Register R_R (.D(part_2_alu_1_alu_out), .en(ld_r), .clk(clk), .Q(data_result), .clr(Reset));
endmodule

module part_2_ALU (
  input  [7:0] input_1,
  input  [7:0] input_2,
  input  ALU_op,
  output [7:0] ALU_out
);

  wire [7:0] adder_1_out, multiplier_1_out;

  Adder adder_1 (.a(input_1), .b(input_2), .out(adder_1_out));  // open: cin, cout
  Multiplier multiplier_1 (.a(input_1), .b(input_2), .out(multiplier_1_out));  // open: cin, cout
  Multiplexer #(.enable("false"), .width(8)) multiplexer_1 (
    .in0(adder_1_out), .in1(multiplier_1_out), .out(ALU_out), .sel(ALU_op));
endmodule

module part_2_state_table (
  input  [3:0] state,
  output ld_a,
  output ld_b,
  output ld_c,
  output ld_x,
  output [1:0] alu_select_a,
  output [1:0] alu_select_b,
  output ld_alu_out,
  output alu_op,
  output ld_r,
  output [3:0] next_state
);

  part_2_ld_a_state_table part_2_ld_a_state_table_1 (.state(state), .ld_a(ld_a));
  part_2_ld_b_state_table part_2_ld_b_state_table_1 (.state(state), .ld_b(ld_b));
  part_2_ld_c_state_table part_2_ld_c_state_table_1 (.state(state), .ld_c(ld_c));
  part_2_ld_x_state_table part_2_ld_x_state_table_1 (.state(state), .ld_x(ld_x));
  part_2_alu_select_a_state_table part_2_alu_select_a_state_table_1 (.state(state), .alu_select_a(alu_select_a));
  part_2_alu_select_b_state_table part_2_alu_select_b_state_table_1 (.state(state), .alu_select_b(alu_select_b));
  part_2_ld_alu_out_state_table part_2_ld_alu_out_state_table_1 (.state(state), .ld_alu_out(ld_alu_out));
  part_2_alu_op_state_table part_2_alu_op_state_table_1 (.state(state), .alu_op(alu_op));
  part_2_ld_r_state_table part_2_ld_r_state_table_1 (.state(state), .ld_r(ld_r));
  part_2_next_state part_2_next_state_1 (.state(state), .next_state(next_state));
endmodule

module part_2_ld_a_state_table (
  input  [3:0] state,
  output ld_a
);

  wire and_1_out, and_2_out, not_1_out, not_2_out, not_3_out, not_4_out, not_5_out;

  not not_1 (not_1_out, state[3]);
  not not_2 (not_2_out, state[2]);
  not not_3 (not_3_out, state[1]);
  not not_4 (not_4_out, state[3]);
  not not_5 (not_5_out, state[0]);
  and and_1 (and_1_out, not_1_out, not_2_out, not_3_out, state[0]);
  and and_2 (and_2_out, not_4_out, state[2], state[1], not_5_out);
  or or_1 (ld_a, and_1_out, and_2_out);
endmodule

module part_2_ld_b_state_table (
  input  [3:0] state,
  output ld_b
);

  wire and_1_out, and_2_out, and_3_out, and_4_out, not_1_out, not_2_out, not_3_out, not_4_out, not_5_out,
       not_6_out, not_7_out, not_8_out, not_9_out;

  not not_1 (not_1_out, state[0]);
  not not_2 (not_2_out, state[2]);
  not not_3 (not_3_out, state[3]);
  not not_4 (not_4_out, state[1]);
  not not_5 (not_5_out, state[3]);
  not not_6 (not_6_out, state[3]);
  not not_7 (not_7_out, state[0]);
  not not_8 (not_8_out, state[1]);
  not not_9 (not_9_out, state[2]);
  and and_1 (and_1_out, not_1_out, state[1], not_2_out, not_3_out);
  and and_2 (and_2_out, state[0], not_4_out, state[2], not_5_out);
  and and_3 (and_3_out, state[0], state[1], state[2], not_6_out);
  and and_4 (and_4_out, not_7_out, not_8_out, not_9_out, state[3]);
  or or_1 (ld_b, and_1_out, and_2_out, and_3_out, and_4_out);
endmodule

module part_2_ld_c_state_table (
  input  [3:0] state,
  output ld_c
);

  wire not_1_out, not_2_out;

  not not_1 (not_1_out, state[2]);
  not not_2 (not_2_out, state[3]);
  and and_1 (ld_c, state[0], state[1], not_1_out, not_2_out);
endmodule

module part_2_ld_x_state_table (
  input  [3:0] state,
  output ld_x
);

  wire not_1_out, not_2_out, not_3_out;

  not not_1 (not_1_out, state[0]);
  not not_2 (not_2_out, state[1]);
  and and_1 (ld_x, not_1_out, not_2_out, state[2], not_3_out);
  not not_3 (not_3_out, state[3]);
endmodule

module part_2_alu_select_a_state_table (
  input  [3:0] state,
  output [1:0] alu_select_a
);

  wire and_2_out, and_3_out, not_1_out, not_2_out, not_3_out, not_4_out, not_5_out;

  and and_1 (alu_select_a[0], state[0], state[1], state[2], not_1_out);
  not not_1 (not_1_out, state[3]);
  and and_2 (and_2_out, state[0], state[1], state[2], not_2_out);
  not not_2 (not_2_out, state[3]);
  not not_3 (not_3_out, state[0]);
  not not_4 (not_4_out, state[1]);
  and and_3 (and_3_out, not_3_out, not_4_out, not_5_out, state[3]);
  not not_5 (not_5_out, state[2]);
  or or_1 (alu_select_a[1], and_2_out, and_3_out);
endmodule

module part_2_alu_select_b_state_table (
  input  [3:0] state,
  output [1:0] alu_select_b
);

  wire and_1_out, and_2_out, and_3_out, and_4_out, and_5_out, not_1_out, not_2_out, not_3_out, not_4_out,
       not_5_out, not_6_out, not_7_out, not_8_out, not_9_out, not_10_out, not_11_out;

  not not_1 (not_1_out, state[1]);
  not not_2 (not_2_out, state[3]);
  not not_3 (not_3_out, state[0]);
  not not_4 (not_4_out, state[3]);
  not not_5 (not_5_out, state[3]);
  not not_6 (not_6_out, state[0]);
  not not_7 (not_7_out, state[1]);
  not not_8 (not_8_out, state[2]);
  not not_9 (not_9_out, state[1]);
  not not_10 (not_10_out, state[2]);
  and and_1 (and_1_out, state[0], not_1_out, state[2], not_2_out);
  and and_2 (and_2_out, not_3_out, state[1], state[2], not_4_out);
  and and_3 (and_3_out, state[0], state[1], state[2], not_5_out);
  and and_4 (and_4_out, not_6_out, not_7_out, not_8_out, state[3]);
  and and_5 (and_5_out, state[0], not_9_out, not_10_out, state[3]);
  and and_6 (alu_select_b[1], state[0], state[1], state[2], not_11_out);
  not not_11 (not_11_out, state[3]);
  or or_1 (alu_select_b[0], and_1_out, and_2_out, and_3_out, and_4_out, and_5_out);
endmodule

module part_2_ld_alu_out_state_table (
  input  [3:0] state,
  output ld_alu_out
);

  wire and_1_out, and_2_out, and_3_out, and_4_out, not_1_out, not_2_out, not_3_out, not_4_out, not_5_out,
       not_6_out, not_7_out, not_8_out;

  not not_1 (not_1_out, state[1]);
  and and_1 (and_1_out, state[0], not_1_out, state[2], not_2_out);
  not not_2 (not_2_out, state[3]);
  not not_3 (not_3_out, state[0]);
  and and_2 (and_2_out, not_3_out, state[1], state[2], not_4_out);
  not not_4 (not_4_out, state[3]);
  and and_3 (and_3_out, state[0], state[1], state[2], not_5_out);
  not not_5 (not_5_out, state[3]);
  not not_6 (not_6_out, state[0]);
  not not_7 (not_7_out, state[1]);
  and and_4 (and_4_out, not_6_out, not_7_out, not_8_out, state[3]);
  not not_8 (not_8_out, state[2]);
  or or_1 (ld_alu_out, and_1_out, and_2_out, and_3_out, and_4_out);
endmodule

module part_2_alu_op_state_table (
  input  [3:0] state,
  output alu_op
);

  wire and_1_out, and_2_out, and_3_out, not_1_out, not_2_out, not_3_out, not_4_out, not_5_out, not_6_out;

  not not_1 (not_1_out, state[1]);
  not not_2 (not_2_out, state[3]);
  not not_3 (not_3_out, state[3]);
  not not_4 (not_4_out, state[0]);
  not not_5 (not_5_out, state[1]);
  not not_6 (not_6_out, state[2]);
  and and_1 (and_1_out, state[0], not_1_out, state[2], not_2_out);
  and and_2 (and_2_out, state[0], state[1], state[2], not_3_out);
  and and_3 (and_3_out, not_4_out, not_5_out, not_6_out, state[3]);
  or or_1 (alu_op, and_1_out, and_2_out, and_3_out);
endmodule

module part_2_ld_r_state_table (
  input  [3:0] state,
  output ld_r
);

  wire not_1_out, not_2_out;

  not not_1 (not_1_out, state[1]);
  not not_2 (not_2_out, state[2]);
  and and_1 (ld_r, state[0], not_1_out, not_2_out, state[3]);
endmodule

module part_2_next_state (
  input  [3:0] state,
  output [3:0] next_state
);

  wire and_1_out, and_2_out, and_3_out, and_4_out, and_5_out, and_6_out, and_7_out, and_8_out, and_9_out,
       and_10_out, and_11_out, and_12_out, and_13_out, and_14_out, and_15_out, not_1_out, not_2_out,
       not_3_out, not_4_out, not_5_out, not_6_out, not_7_out, not_8_out, not_9_out, not_10_out, not_11_out,
       not_12_out, not_13_out, not_14_out, not_15_out, not_16_out, not_17_out, not_18_out, not_19_out,
       not_20_out, not_21_out, not_22_out, not_23_out, not_24_out, not_25_out, not_26_out, not_27_out,
       not_28_out, not_29_out, not_30_out, not_31_out, not_32_out, not_33_out, not_34_out, not_35_out,
       not_36_out, not_37_out, not_38_out;

  not not_1 (not_1_out, state[0]);
  not not_2 (not_2_out, state[3]);
  not not_3 (not_3_out, state[0]);
  not not_4 (not_4_out, state[1]);
  not not_5 (not_5_out, state[3]);
  not not_6 (not_6_out, state[0]);
  not not_7 (not_7_out, state[1]);
  not not_8 (not_8_out, state[2]);
  not not_9 (not_9_out, state[0]);
  not not_10 (not_10_out, state[1]);
  not not_11 (not_11_out, state[2]);
  not not_12 (not_12_out, state[3]);
  not not_13 (not_13_out, state[0]);
  not not_14 (not_14_out, state[2]);
  not not_15 (not_15_out, state[3]);
  not not_16 (not_16_out, state[1]);
  not not_17 (not_17_out, state[2]);
  not not_18 (not_18_out, state[3]);
  not not_19 (not_19_out, state[0]);
  not not_20 (not_20_out, state[2]);
  not not_21 (not_21_out, state[3]);
  not not_22 (not_22_out, state[1]);
  not not_23 (not_23_out, state[3]);
  not not_24 (not_24_out, state[0]);
  not not_25 (not_25_out, state[3]);
  not not_26 (not_26_out, state[2]);
  not not_27 (not_27_out, state[3]);
  not not_28 (not_28_out, state[0]);
  not not_29 (not_29_out, state[1]);
  not not_30 (not_30_out, state[3]);
  not not_31 (not_31_out, state[1]);
  not not_32 (not_32_out, state[3]);
  not not_33 (not_33_out, state[0]);
  not not_34 (not_34_out, state[3]);
  not not_35 (not_35_out, state[3]);
  not not_36 (not_36_out, state[0]);
  not not_37 (not_37_out, state[1]);
  not not_38 (not_38_out, state[2]);
  and and_1 (and_1_out, not_1_out, state[1], state[2], not_2_out);
  and and_2 (and_2_out, not_3_out, not_4_out, state[2], not_5_out);
  and and_3 (and_3_out, not_6_out, not_7_out, not_8_out, state[3]);
  and and_4 (and_4_out, not_9_out, not_10_out, not_11_out, not_12_out);
  and and_5 (and_5_out, not_13_out, state[1], not_14_out, not_15_out);
  and and_6 (and_6_out, state[0], not_16_out, not_17_out, not_18_out);
  and and_7 (and_7_out, not_19_out, state[1], not_20_out, not_21_out);
  and and_8 (and_8_out, state[0], not_22_out, state[2], not_23_out);
  and and_9 (and_9_out, not_24_out, state[1], state[2], not_25_out);
  and and_10 (and_10_out, state[0], state[1], not_26_out, not_27_out);
  and and_11 (and_11_out, not_28_out, not_29_out, state[2], not_30_out);
  and and_12 (and_12_out, state[0], not_31_out, state[2], not_32_out);
  and and_13 (and_13_out, not_33_out, state[1], state[2], not_34_out);
  and and_14 (and_14_out, state[0], state[1], state[2], not_35_out);
  and and_15 (and_15_out, not_36_out, not_37_out, not_38_out, state[3]);
  or or_1 (next_state[0], and_4_out, and_3_out, and_1_out, and_2_out, and_5_out);
  or or_2 (next_state[1], and_6_out, and_8_out, and_9_out, and_7_out);
  or or_3 (next_state[2], and_10_out, and_12_out, and_13_out, and_11_out);
  or or_4 (next_state[3], and_14_out, and_15_out);
endmodule

module part_2_FSM (
  input  [7:0] data_in,
  input  Enable,
  input  Reset
);

  wire Clk_out, not_1_out, part_2_state_table_1_alu_op, part_2_state_table_1_ld_a,
       part_2_state_table_1_ld_alu_out, part_2_state_table_1_ld_b, part_2_state_table_1_ld_c,
       part_2_state_table_1_ld_r, part_2_state_table_1_ld_x;
  wire [1:0] part_2_state_table_1_alu_select_a, part_2_state_table_1_alu_select_b;
  wire [3:0] part_2_state_table_1_next_state, register_1_q;
  wire [7:0] part_2_datapath_1_data_result, part_2_datapath_1_r_a_val, part_2_datapath_1_r_b_val,
       part_2_datapath_1_r_c_val, part_2_datapath_1_r_x_val;

  part_2_state_table part_2_state_table_1 (
    .state(register_1_q), .ld_a(part_2_state_table_1_ld_a), .ld_b(part_2_state_table_1_ld_b),
    .ld_c(part_2_state_table_1_ld_c), .ld_x(part_2_state_table_1_ld_x),
    .alu_select_a(part_2_state_table_1_alu_select_a), .alu_select_b(part_2_state_table_1_alu_select_b),
    .ld_alu_out(part_2_state_table_1_ld_alu_out), .alu_op(part_2_state_table_1_alu_op),
    .ld_r(part_2_state_table_1_ld_r), .next_state(part_2_state_table_1_next_state));
  Register #(.width(4)) register_1 (
    .D(part_2_state_table_1_next_state), .en(Enable), .clk(Clk_out), .Q(register_1_q), .clr(not_1_out));
  not not_1 (not_1_out, Reset);
  Clock Clk (.out(Clk_out));
  Hex_Digit_Display hex_digit_display_1 (.value(data_in[7:4]));  // open: dp
  Hex_Digit_Display hex_digit_display_2 (.value(data_in[3:0]));  // open: dp
  part_2_datapath part_2_datapath_1 (
    .ld_alu_out(part_2_state_table_1_ld_alu_out), .data_in(data_in), .clk(Clk_out),
    .ld_c(part_2_state_table_1_ld_c), .ld_x(part_2_state_table_1_ld_x), .ld_a(part_2_state_table_1_ld_a),
    .ld_b(part_2_state_table_1_ld_b), .Reset(not_1_out), .alu_select_a(part_2_state_table_1_alu_select_a),
    .alu_select_b(part_2_state_table_1_alu_select_b), .alu_op(part_2_state_table_1_alu_op),
    .ld_r(part_2_state_table_1_ld_r), .R_B_val(part_2_datapath_1_r_b_val),
    .R_A_val(part_2_datapath_1_r_a_val), .R_X_val(part_2_datapath_1_r_x_val),
    .R_C_val(part_2_datapath_1_r_c_val), .data_result(part_2_datapath_1_data_result));
  Hex_Digit_Display hex_digit_display_3 (.value(part_2_datapath_1_r_b_val[7:4]));  // open: dp
  Hex_Digit_Display hex_digit_display_4 (.value(part_2_datapath_1_r_b_val[3:0]));  // open: dp
  Hex_Digit_Display hex_digit_display_5 (.value(part_2_datapath_1_r_c_val[7:4]));  // open: dp
  Hex_Digit_Display hex_digit_display_6 (.value(part_2_datapath_1_data_result[7:4]));  // open: dp
  Hex_Digit_Display hex_digit_display_7 (.value(part_2_datapath_1_r_a_val[7:4]));  // open: dp
  Hex_Digit_Display hex_digit_display_8 (.value(part_2_datapath_1_r_x_val[7:4]));  // open: dp
  Hex_Digit_Display hex_digit_display_9 (.value(part_2_datapath_1_r_x_val[3:0]));  // open: dp
  Hex_Digit_Display hex_digit_display_10 (.value(part_2_datapath_1_r_c_val[3:0]));  // open: dp
  Hex_Digit_Display hex_digit_display_11 (.value(part_2_datapath_1_data_result[3:0]));  // open: dp
  LED led_1 (.in(part_2_datapath_1_data_result[0]));
  LED led_2 (.in(part_2_datapath_1_data_result[1]));
  LED led_3 (.in(part_2_datapath_1_data_result[2]));
  LED led_4 (.in(part_2_datapath_1_data_result[3]));
  LED led_5 (.in(part_2_datapath_1_data_result[4]));
  LED led_6 (.in(part_2_datapath_1_data_result[5]));
  LED led_7 (.in(part_2_datapath_1_data_result[6]));
  LED led_8 (.in(part_2_datapath_1_data_result[7]));
  Hex_Digit_Display hex_digit_display_12 (.value(part_2_datapath_1_r_a_val[3:0]));  // open: dp
endmodule

module A (
  input  W,
  output [2:0] O
);

  Multiplexer #(.enable("false"), .width(3)) multiplexer_1 (.in0(3'b000), .in1(3'b001), .out(O), .sel(W));
endmodule

module B (
  input  W,
  output [2:0] O
);

  Multiplexer #(.enable("false"), .width(3)) multiplexer_1 (.in0(3'b000), .in1(3'b011), .out(O), .sel(W));
endmodule

module C (
  input  W,
  output [2:0] O
);

  Multiplexer #(.enable("false"), .width(3)) multiplexer_1 (.in0(3'b110), .in1(3'b111), .out(O), .sel(W));
endmodule

module D (
  input  W,
  output [2:0] O
);

  Multiplexer #(.enable("false"), .width(3)) multiplexer_1 (.in0(3'b110), .in1(3'b101), .out(O), .sel(W));
endmodule

module E (
  input  W,
  output [2:0] O
);

  Multiplexer #(.enable("false"), .width(3)) multiplexer_1 (.in0(3'b000), .in1(3'b010), .out(O), .sel(W));
endmodule

module F (
  input  W,
  output [2:0] O
);

  Multiplexer #(.enable("false"), .width(3)) multiplexer_1 (.in0(3'b110), .in1(3'b101), .out(O), .sel(W));
endmodule

module G (
  input  W,
  output [2:0] O
);

  Multiplexer #(.enable("false"), .width(3)) multiplexer_1 (.in0(3'b000), .in1(3'b011), .out(O), .sel(W));
endmodule

module part1_output (
  input  [2:0] Q,
  output O
);

  Multiplexer #(.enable("false"), .select(3)) multiplexer_1 (
    .in0(1'b0), .in1(1'b0), .in2(1'b1), .in3(1'b0), .in4(1'b0), .in5(1'b1), .in6(1'b0), .in7(1'b0), .out(O),
    .sel(Q));
endmodule
