// Logisim project part1.circ as structural Verilog: 3 circuits, main circuit main
module main (
  input  W,
  input  clear,
  input  O,
  input  Enable
);

  wire clock_1_out, register_1_q, register_2_q;
  wire [3:0] datain_1_o, ram_1_dout;
  wire [4:0] add_1_out_4;

  Clock clock_1 (.out(clock_1_out));
  Register #(.width(1)) register_1 (.D(W), .clk(clock_1_out), .Q(register_1_q));  // open: en, clr
  Register #(.width(1)) register_2 (.D(O), .clk(clock_1_out), .Q(register_2_q));  // open: en, clr
  add add_1 (.clear(clear), .enable(Enable), .clockk(clock_1_out), .out_4(add_1_out_4));
  datain datain_1 (.clear(clear), .enable(Enable), .clockk(clock_1_out), .O(datain_1_o));
  RAM #(.addrWidth(5), .dataWidth(4)) ram_1 (
    .addr(add_1_out_4), .we(register_1_q), .oe(register_2_q), .clk(clock_1_out), .din(datain_1_o),
    .dout(ram_1_dout));
  Hex_Digit_Display hex_digit_display_1 (.value(ram_1_dout));  // open: dp
endmodule

module datain (
  input  clear,
  input  enable,
  input  clockk,
  output [3:0] O
);

  wire and_1_out, not_1_out, or_1_out;

  not not_1 (not_1_out, enable);
  or or_1 (or_1_out, and_1_out, not_1_out);
  Counter #(.max('hf), .width(4)) counter_1 (
    .clr(clear), .load(or_1_out), .up(1'b1), .clk(clockk), .D(4'b0000), .Q(O));  // open: count, carry
  and and_1 (and_1_out, O[3], O[2], O[1], O[0]);
endmodule

module add (
  input  clear,
  input  enable,
  input  clockk,
  output [4:0] out_4
);

  wire not_1_out, or_1_out;

  not not_1 (not_1_out, enable);
  buf or_1 (or_1_out, not_1_out);  // OR_Gate
  Counter #(.max('h1f), .width(5)) counter_1 (
    .clr(clear), .load(or_1_out), .up(1'b1), .clk(clockk), .D({5{1'b0}}), .Q(out_4));  // open: count, carry
endmodule
