// Logisim project part2.circ as structural Verilog: 9 circuits, main circuit main
module main (
  input  w,
  input  [6:0] x,
  input  clear,
  input  [6:0] y
);

  wire clk_out, fsm_1_enablex, fsm_1_enabley, fsm_1_we;
  wire [6:0] adder_1_out, adder_2_out, register_1_q, register_2_q, xconter_1_out_4, yconter_1_out_4;
  wire [23:0] register_3_q;

  FSM fsm_1 (
    .W(w), .x(xconter_1_out_4), .y(yconter_1_out_4), .enablex(fsm_1_enablex), .enabley(fsm_1_enabley),
    .WE(fsm_1_we));
  Register #(.width(7)) register_1 (.D(x), .en(w), .clk(clk_out), .Q(register_1_q));  // open: clr
  Register #(.width(7)) register_2 (.D(y), .en(w), .clk(clk_out), .Q(register_2_q));  // open: clr
  xconter xconter_1 (.clear(clear), .enable(fsm_1_enablex), .clockk(clk_out), .out_4(xconter_1_out_4));
  yconter yconter_1 (.clear(clear), .enable(fsm_1_enabley), .clockk(clk_out), .out_4(yconter_1_out_4));
  Register #(.width(24)) register_3 (.D(24'hb1), .en(w), .clk(clk_out), .Q(register_3_q));  // open: clr
  Adder #(.width(7)) adder_1 (.a(xconter_1_out_4), .b(register_1_q), .out(adder_1_out));  // open: cin, cout
  Adder #(.width(7)) adder_2 (.a(yconter_1_out_4), .b(register_2_q), .out(adder_2_out));  // open: cin, cout
  Clock clk (.out(clk_out));
  // RGB_Video rgb_video_1: pin names not known; wires that end beside it: clear, clk_out, fsm_1_we, adder_1_out, adder_2_out, register_3_q
endmodule

module FSM (
  input  W,
  input  [6:0] x,
  input  [6:0] y,
  output enablex,
  output enabley,
  output WE
);

  statetable statetable_1 (.w(W), .x(x), .y(y), .Ex(enablex), .Ey(enabley), .WR(WE));
endmodule

module xconter (
  input  clear,
  input  enable,
  input  clockk,
  output [6:0] out_4
);

  wire not_1_out, or_1_out;

  not not_1 (not_1_out, enable);
  buf or_1 (or_1_out, not_1_out);  // OR_Gate
  Counter #(.max('hf), .width(4)) counter_1 (
    .clr(clear), .load(or_1_out), .up(1'b1), .clk(clockk), .D(4'b0000), .Q(out_4[3:0]));  // open: count, carry

  assign out_4[6:4] = 3'b000;
endmodule

module yconter (
  input  clear,
  input  enable,
  input  clockk,
  output [6:0] out_4
);

  wire and_1_out, not_1_out, not_2_out, not_3_out, not_4_out, not_5_out, or_1_out;
  wire [3:0] multiplexer_1_out;

  buf or_1 (or_1_out, not_1_out);  // OR_Gate
  not not_1 (not_1_out, enable);
  Multiplexer #(.enable("false"), .width(4)) multiplexer_1 (
    .in0(4'b0000), .in1(out_4[3:0]), .out(multiplexer_1_out), .sel(not_5_out));
  Counter #(.max('hf), .width(4)) counter_1 (
    .clr(clear), .load(or_1_out), .up(1'b1), .clk(clockk), .D(multiplexer_1_out), .Q(out_4[3:0]));  // open: count, carry
  not not_2 (not_2_out, 1'b0);
  not not_3 (not_3_out, 1'b0);
  not not_4 (not_4_out, 1'b0);
  and and_1 (and_1_out, out_4[0], out_4[1], out_4[2], out_4[3], not_2_out, not_3_out, not_4_out);
  not not_5 (not_5_out, and_1_out);

  assign out_4[6:4] = 3'b000;
endmodule

module statea00 (
  input  [1:0] state,
  output Ex,
  output Ey,
  output Wr
);


  assign Ex = 1'b0;
  assign Ey = 1'b0;
  assign Wr = 1'b0;
endmodule

module stateb01 (
  input  [1:0] state,
  output Ex,
  output Ey,
  output wr
);


  assign Ex = state[0];
  assign Ey = 1'b0;
  assign wr = state[0];
endmodule

module statec11 (
  input  [1:0] state,
  output Ex,
  output Ey,
  output wr
);

  and and_1 (Ex, state[1], state[0]);

  assign Ey = Ex;
  assign wr = Ex;
endmodule

module statetable (
  input  w,
  input  [6:0] x,
  input  [6:0] y,
  output Ex,
  output Ey,
  output WR
);

  wire statea00_1_ex, statea00_1_ey, statea00_1_wr, stateb01_1_ex, stateb01_1_ey, stateb01_1_wr,
       statec11_1_ex, statec11_1_ey, statec11_1_wr;
  wire [1:0] nextstate_1_state;

  nextstate nextstate_1 (.W(w), .x(x), .y(y), .state(nextstate_1_state));
  statea00 statea00_1 (.state(nextstate_1_state), .Ex(statea00_1_ex), .Ey(statea00_1_ey), .Wr(statea00_1_wr));
  stateb01 stateb01_1 (.state(nextstate_1_state), .Ex(stateb01_1_ex), .Ey(stateb01_1_ey), .wr(stateb01_1_wr));
  statec11 statec11_1 (.state(nextstate_1_state), .Ex(statec11_1_ex), .Ey(statec11_1_ey), .wr(statec11_1_wr));
  or or_1 (Ex, statea00_1_ex, stateb01_1_ex, statec11_1_ex);
  or or_2 (WR, statea00_1_wr, stateb01_1_wr, statec11_1_wr);
  or or_3 (Ey, statea00_1_ey, stateb01_1_ey, statec11_1_ey);
endmodule

module nextstate (
  input  W,
  input  [6:0] x,
  input  [6:0] y,
  output [1:0] state
);

  wire and_1_out, and_2_out, not_1_out, not_2_out, not_3_out, not_4_out, not_5_out, not_6_out, not_7_out,
       not_8_out;

  and and_1 (and_1_out, x[0], x[1], x[2], x[3], not_1_out, not_2_out, not_3_out);
  not not_1 (not_1_out, x[4]);
  not not_2 (not_2_out, x[5]);
  not not_3 (not_3_out, x[6]);
  and and_2 (and_2_out, y[0], y[1], y[2], y[3], not_4_out, not_5_out, not_6_out);
  not not_4 (not_4_out, y[4]);
  not not_5 (not_5_out, y[5]);
  not not_6 (not_6_out, y[6]);
  and and_3 (state[0], W, not_7_out);
  not not_7 (not_7_out, and_2_out);
  and and_4 (state[1], and_1_out, not_8_out);
  not not_8 (not_8_out, and_2_out);
endmodule
